// Logisim project computing_machine.circ as structural Verilog: 15 circuits, main circuit main
module main (
);

  wire clock_generator_1_clk, core_1_alu_en, core_1_br_oe, core_1_br_we, core_1_cr_ce, core_1_cr_oe,
       core_1_cr_we, core_1_hlt, core_1_ip_ce, core_1_ip_oe, core_1_ip_we, core_1_mem_oe, core_1_mem_we,
       core_1_regs_oe, core_1_regs_we, core_1_sg_clr, cr_1_emp, voltage_source_1_gnd, voltage_source_1_vcc;
  wire [1:0] core_1_alu_mode;
  wire [2:0] core_1_alu_opsel, core_1_ir_ie, core_1_regs_a;
  wire [4:0] alu_1_state;
  wire [7:0] cr_1_o;
  wire [10:0] core_1_a, ip_1_ab;
  wire [15:0] signal_generator_1_cb;
  wire [23:0] ir_1_command;

  IP ip_1 (
    .VCC(voltage_source_1_vcc), .CE(core_1_ip_ce), .CLK(clock_generator_1_clk), .WE(1'b0), .OE(1'b1),
    .GND(voltage_source_1_gnd), .AB(ip_1_ab));
  CR cr_1 (
    .GND(voltage_source_1_gnd), .CLK(clock_generator_1_clk), .CE(1'b0), .WE(1'b0),
    .VCC(voltage_source_1_vcc), .OE(1'b0), .I(cr_1_o), .EMP(cr_1_emp), .O(cr_1_o));
  registers registers_1 (
    .OE(1'b0), .I(cr_1_o), .VCC(voltage_source_1_vcc), .CLK(clock_generator_1_clk),
    .GND(voltage_source_1_gnd), .A(3'b000), .WE(1'b0), .O(cr_1_o));
  LED led_1 (.in(ip_1_ab[10]));
  LED led_2 (.in(ip_1_ab[9]));
  LED led_3 (.in(ip_1_ab[8]));
  LED led_4 (.in(ip_1_ab[7]));
  LED led_5 (.in(ip_1_ab[6]));
  LED led_6 (.in(ip_1_ab[5]));
  LED led_7 (.in(ip_1_ab[4]));
  LED led_8 (.in(ip_1_ab[3]));
  clock_generator clock_generator_1 (
    .VCC(voltage_source_1_vcc), .GND(voltage_source_1_gnd), .HLT(1'b0), .CLK(clock_generator_1_clk));
  memory memory_1 (
    .VCC(voltage_source_1_vcc), .GND(voltage_source_1_gnd), .WE(1'b0), .OE(1'b1),
    .CLK(clock_generator_1_clk), .I(cr_1_o), .A(ip_1_ab), .O(cr_1_o));
  ALU alu_1 (
    .MODE(2'b00), .OPSEL(3'b000), .I(cr_1_o), .EN(1'b0), .CLK(clock_generator_1_clk),
    .VCC(voltage_source_1_vcc), .GND(voltage_source_1_gnd), .STATE(alu_1_state), .O(cr_1_o));
  LED led_9 (.in(ip_1_ab[2]));
  LED led_10 (.in(ip_1_ab[1]));
  LED led_11 (.in(ip_1_ab[0]));
  LED led_12 (.in(cr_1_emp));
  LED AE (.in(alu_1_state[3]));
  LED LE (.in(alu_1_state[1]));
  LED A (.in(alu_1_state[4]));
  LED E (.in(alu_1_state[2]));
  LED led_13 (.in(cr_1_o[7]));
  LED led_14 (.in(cr_1_o[6]));
  LED led_15 (.in(cr_1_o[5]));
  LED L (.in(alu_1_state[0]));
  LED led_16 (.in(cr_1_o[4]));
  LED led_17 (.in(cr_1_o[3]));
  LED led_18 (.in(cr_1_o[2]));
  LED led_19 (.in(cr_1_o[1]));
  LED led_20 (.in(cr_1_o[0]));
  LED led_21 (.in(signal_generator_1_cb[15]));
  LED led_22 (.in(signal_generator_1_cb[14]));
  LED led_23 (.in(signal_generator_1_cb[13]));
  LED led_24 (.in(signal_generator_1_cb[12]));
  LED led_25 (.in(signal_generator_1_cb[11]));
  core core_1 (
    .VCC(voltage_source_1_vcc), .CLK(clock_generator_1_clk), .GND(voltage_source_1_gnd),
    .CB(signal_generator_1_cb), .BR_WE(core_1_br_we), .BR_OE(core_1_br_oe), .A(core_1_a), .HLT(core_1_hlt),
    .IP_WE(core_1_ip_we), .IP_OE(core_1_ip_oe), .MEM_WE(core_1_mem_we), .MEM_OE(core_1_mem_oe),
    .CR_WE(core_1_cr_we), .CR_OE(core_1_cr_oe), .CR_CE(core_1_cr_ce), .REGS_WE(core_1_regs_we),
    .REGS_OE(core_1_regs_oe), .REGS_A(core_1_regs_a), .ALU_MODE(core_1_alu_mode),
    .ALU_OPSEL(core_1_alu_opsel), .ALU_EN(core_1_alu_en), .SG_CLR(core_1_sg_clr), .IR_IE(core_1_ir_ie),
    .IP_CE(core_1_ip_ce));  // open: CR_EMP, ALU_STATE, IR_CMD
  LED led_26 (.in(signal_generator_1_cb[10]));
  LED led_27 (.in(signal_generator_1_cb[9]));
  LED led_28 (.in(signal_generator_1_cb[8]));
  LED led_29 (.in(signal_generator_1_cb[7]));
  LED led_30 (.in(signal_generator_1_cb[6]));
  LED led_31 (.in(signal_generator_1_cb[5]));
  LED led_32 (.in(signal_generator_1_cb[4]));
  LED led_33 (.in(signal_generator_1_cb[3]));
  voltage_source voltage_source_1 (.ON_OFF(1'b1), .VCC(voltage_source_1_vcc), .GND(voltage_source_1_gnd));
  LED led_34 (.in(signal_generator_1_cb[2]));
  LED led_35 (.in(signal_generator_1_cb[1]));
  LED led_36 (.in(signal_generator_1_cb[0]));
  signal_generator signal_generator_1 (
    .CLK(clock_generator_1_clk), .CLR(core_1_sg_clr), .GND(voltage_source_1_gnd), .VCC(voltage_source_1_vcc),
    .CB(signal_generator_1_cb));
  IR ir_1 (
    .I(cr_1_o), .VCC(voltage_source_1_vcc), .CLK(clock_generator_1_clk), .IE(core_1_ir_ie),
    .GND(voltage_source_1_gnd), .COMMAND(ir_1_command));
  RX BR (
    .CLK(clock_generator_1_clk), .WE(1'b0), .OE(1'b0), .GND(voltage_source_1_gnd),
    .VCC(voltage_source_1_vcc), .O(cr_1_o));  // open: I
  LED led_37 (.in(ir_1_command[23]));
  Hex_Digit_Display hex_digit_display_1 (.value(ir_1_command[23:20]));  // open: dp
  LED led_38 (.in(ir_1_command[19]));
  LED led_39 (.in(ir_1_command[22]));
  LED led_40 (.in(ir_1_command[21]));
  LED led_41 (.in(ir_1_command[20]));
  Hex_Digit_Display hex_digit_display_2 (.value(ir_1_command[19:16]));  // open: dp
  LED led_42 (.in(ir_1_command[18]));
  LED led_43 (.in(ir_1_command[17]));
  LED led_44 (.in(ir_1_command[16]));
  LED led_45 (.in(ir_1_command[15]));
  Hex_Digit_Display hex_digit_display_3 (.value(ir_1_command[15:12]));  // open: dp
  LED led_46 (.in(ir_1_command[11]));
  LED led_47 (.in(ir_1_command[14]));
  LED led_48 (.in(ir_1_command[13]));
  LED led_49 (.in(ir_1_command[12]));
  Hex_Digit_Display hex_digit_display_4 (.value(ir_1_command[11:8]));  // open: dp
  LED led_50 (.in(ir_1_command[10]));
  LED led_51 (.in(ir_1_command[9]));
  LED led_52 (.in(ir_1_command[8]));
  LED led_53 (.in(ir_1_command[7]));
  Hex_Digit_Display hex_digit_display_5 (.value(ir_1_command[7:4]));  // open: dp
  LED led_54 (.in(ir_1_command[3]));
  LED led_55 (.in(ir_1_command[6]));
  LED led_56 (.in(ir_1_command[5]));
  LED led_57 (.in(ir_1_command[4]));
  Hex_Digit_Display hex_digit_display_6 (.value(ir_1_command[3:0]));  // open: dp
  LED led_58 (.in(ir_1_command[2]));
  LED led_59 (.in(ir_1_command[1]));
  LED led_60 (.in(ir_1_command[0]));
endmodule

module hc299 (
  input  I0,
  input  I1,
  input  I2,
  input  VCC,
  input  I3,
  input  I4,
  input  GND,
  input  I5,
  input  I6,
  input  I7,
  input  Dsl,
  input  Dsr,
  input  nOE1,
  input  nOE2,
  input  S0,
  input  S1,
  input  CP,
  input  nMR,
  output O0,
  output O1,
  output O2,
  output O3,
  output O4,
  output O5,
  output O6,
  output O7,
  output Q7,
  output Q0
);

  wire nand_1_out, nand_2_out, not_1_out, not_2_out, not_3_out, not_4_out, not_5_out, not_6_out;
  wire [7:0] controlled_buffer_1_out, register_1_q;

  // NoConnect on VCC
  // NoConnect on GND
  // NoConnect on Dsl
  // NoConnect on Dsr
  not not_1 (not_1_out, nOE1);
  not not_2 (not_2_out, nOE2);
  nand nand_1 (nand_1_out, not_1_out, nand_2_out, not_2_out);
  nand nand_2 (nand_2_out, S0, S1);
  not not_3 (not_3_out, nand_2_out);
  assign controlled_buffer_1_out = not_3_out ? {I7, I6, I5, I4, I3, I2, I1, I0} : 8'bz;  // Controlled_Buffer controlled_buffer_1
  Register register_1 (.D(controlled_buffer_1_out), .en(not_4_out), .clk(CP), .Q(register_1_q), .clr(not_5_out));
  not not_4 (not_4_out, nand_2_out);
  not not_5 (not_5_out, nMR);
  assign {O7, O6, O5, O4, O3, O2, O1, O0} = not_6_out ? register_1_q : 8'bz;  // Controlled_Buffer controlled_buffer_2
  not not_6 (not_6_out, nand_1_out);

  assign Q0 = 1'b0;
  assign Q7 = 1'b0;
endmodule

module signal_generator (
  input  VCC,
  input  CLK,
  input  CLR,
  input  GND,
  output [15:0] CB
);

  wire n74161_1_pin11, n74161_1_pin12, n74161_1_pin13, n74161_1_pin14, n74161_1_pin15, pull_resistor_1_node,
       pull_resistor_2_node;
  wire [15:0] hc154en_1_ny0;

  Pull_Resistor #(.pull(1)) pull_resistor_1 (.node(pull_resistor_1_node));
  Transistor #(.\type ("n")) transistor_1 (.in(GND), .out(pull_resistor_1_node), .gate(CLK));
  Pull_Resistor #(.pull(1)) pull_resistor_2 (.node(pull_resistor_2_node));
  Transistor #(.\type ("n")) transistor_2 (.in(GND), .out(pull_resistor_2_node), .gate(CLR));
  hc154en hc154en_1 (
    .VCC(VCC), .GND(GND), .A0(n74161_1_pin14), .A1(n74161_1_pin13), .A2(n74161_1_pin12), .A3(n74161_1_pin11),
    .nE0(GND), .nE1(GND), .nY0(hc154en_1_ny0[0]), .nY1(hc154en_1_ny0[1]), .nY2(hc154en_1_ny0[2]),
    .nY3(hc154en_1_ny0[3]), .nY4(hc154en_1_ny0[4]), .nY5(hc154en_1_ny0[5]), .nY6(hc154en_1_ny0[6]),
    .nY7(hc154en_1_ny0[7]), .nY8(hc154en_1_ny0[8]), .nY9(hc154en_1_ny0[9]), .nY10(hc154en_1_ny0[10]),
    .nY11(hc154en_1_ny0[11]), .nY12(hc154en_1_ny0[12]), .nY13(hc154en_1_ny0[13]), .nY14(hc154en_1_ny0[14]),
    .nY15(hc154en_1_ny0[15]));
  Pull_Resistor #(.pull(1)) pull_resistor_3 (.node(CB[15]));
  Pull_Resistor #(.pull(1)) pull_resistor_4 (.node(CB[14]));
  Transistor #(.\type ("n")) transistor_3 (.in(GND), .out(CB[15]), .gate(hc154en_1_ny0[15]));
  Transistor #(.\type ("n")) transistor_4 (.in(GND), .out(CB[14]), .gate(hc154en_1_ny0[14]));
  LED led_1 (.in(n74161_1_pin15));
  Pull_Resistor #(.pull(1)) pull_resistor_5 (.node(CB[13]));
  Transistor #(.\type ("n")) transistor_5 (.in(GND), .out(CB[13]), .gate(hc154en_1_ny0[13]));
  Transistor #(.\type ("n")) transistor_6 (.in(GND), .out(CB[12]), .gate(hc154en_1_ny0[12]));
  _74161 u_74161_1 (
    .pin1(pull_resistor_2_node), .pin2(pull_resistor_1_node), .pin3(VCC), .pin4(VCC), .pin5(VCC), .pin6(VCC),
    .pin7(VCC), .pin15(n74161_1_pin15), .pin14(n74161_1_pin14), .pin13(n74161_1_pin13),
    .pin12(n74161_1_pin12), .pin11(n74161_1_pin11), .pin10(VCC), .pin9(VCC));
  Pull_Resistor #(.pull(1)) pull_resistor_6 (.node(CB[12]));
  Pull_Resistor #(.pull(1)) pull_resistor_7 (.node(CB[11]));
  Transistor #(.\type ("n")) transistor_7 (.in(GND), .out(CB[11]), .gate(hc154en_1_ny0[11]));
  Pull_Resistor #(.pull(1)) pull_resistor_8 (.node(CB[10]));
  Pull_Resistor #(.pull(1)) pull_resistor_9 (.node(CB[9]));
  Transistor #(.\type ("n")) transistor_8 (.in(GND), .out(CB[10]), .gate(hc154en_1_ny0[10]));
  Transistor #(.\type ("n")) transistor_9 (.in(GND), .out(CB[9]), .gate(hc154en_1_ny0[9]));
  Pull_Resistor #(.pull(1)) pull_resistor_10 (.node(CB[8]));
  Transistor #(.\type ("n")) transistor_10 (.in(GND), .out(CB[8]), .gate(hc154en_1_ny0[8]));
  Pull_Resistor #(.pull(1)) pull_resistor_11 (.node(CB[6]));
  Pull_Resistor #(.pull(1)) pull_resistor_12 (.node(CB[7]));
  Transistor #(.\type ("n")) transistor_11 (.in(GND), .out(CB[6]), .gate(hc154en_1_ny0[6]));
  Transistor #(.\type ("n")) transistor_12 (.in(GND), .out(CB[7]), .gate(hc154en_1_ny0[7]));
  Pull_Resistor #(.pull(1)) pull_resistor_13 (.node(CB[5]));
  Transistor #(.\type ("n")) transistor_13 (.in(GND), .out(CB[5]), .gate(hc154en_1_ny0[5]));
  Transistor #(.\type ("n")) transistor_14 (.in(GND), .out(CB[4]), .gate(hc154en_1_ny0[4]));
  Pull_Resistor #(.pull(1)) pull_resistor_14 (.node(CB[4]));
  Pull_Resistor #(.pull(1)) pull_resistor_15 (.node(CB[3]));
  Transistor #(.\type ("n")) transistor_15 (.in(GND), .out(CB[3]), .gate(hc154en_1_ny0[3]));
  Pull_Resistor #(.pull(1)) pull_resistor_16 (.node(CB[2]));
  Pull_Resistor #(.pull(1)) pull_resistor_17 (.node(CB[1]));
  Transistor #(.\type ("n")) transistor_16 (.in(GND), .out(CB[2]), .gate(hc154en_1_ny0[2]));
  Transistor #(.\type ("n")) transistor_17 (.in(GND), .out(CB[1]), .gate(hc154en_1_ny0[1]));
  Pull_Resistor #(.pull(1)) pull_resistor_18 (.node(CB[0]));
  Transistor #(.\type ("n")) transistor_18 (.in(GND), .out(CB[0]), .gate(hc154en_1_ny0[0]));

  // Notes on the sheet:
  //   not
  //   not
endmodule

module IP (
  input  VCC,
  input  CE,
  input  CLK,
  input  WE,
  input  OE,
  input  GND,
  output [10:0] AB
);

  wire n74161_1_pin1, n74161_1_pin6, n74161_1_pin7, n74161_1_pin10, n74161_1_pin11, n74161_1_pin12,
       n74161_1_pin13, n74161_1_pin14, n74161_1_pin15, n74161_2_pin1, n74161_2_pin10, n74161_2_pin11,
       n74161_2_pin12, n74161_2_pin13, n74161_2_pin14, n74161_3_pin1, n74161_3_pin10, n74161_3_pin11,
       n74161_3_pin12, n74161_3_pin13, n74161_3_pin14, n74245_1_pin5, n74245_1_pin6, n74245_1_pin7,
       n74245_1_pin8, n74245_1_pin9, n74245_1_pin11, n74245_1_pin12, n74245_1_pin13, n74245_1_pin14,
       n74245_1_pin15, n74245_1_pin19, n74245_2_pin19, pull_resistor_1_node;

  Pull_Resistor #(.pull(1)) pull_resistor_1 (.node(pull_resistor_1_node));
  Transistor #(.\type ("n")) transistor_1 (.in(GND), .out(pull_resistor_1_node), .gate(CLK));
  Transistor #(.\type ("n")) transistor_2 (.in(GND), .out(pull_resistor_1_node), .gate(WE));
  // NoConnect on n74161_1_pin6
  // NoConnect on n74161_1_pin11
  _74161 u_74161_1 (
    .pin1(n74161_1_pin1), .pin2(CLK), .pin3(AB[2]), .pin4(AB[1]), .pin5(AB[0]), .pin6(n74161_1_pin6),
    .pin7(n74161_1_pin7), .pin15(n74161_1_pin15), .pin14(n74161_1_pin14), .pin13(n74161_1_pin13),
    .pin12(n74161_1_pin12), .pin11(n74161_1_pin11), .pin10(n74161_1_pin10), .pin9(pull_resistor_1_node));
  // NoConnect on n74161_1_pin15
  // NoConnect on n74245_1_pin9
  // NoConnect on n74245_1_pin8
  // NoConnect on n74245_1_pin7
  // NoConnect on n74245_1_pin11
  // NoConnect on n74245_1_pin12
  // NoConnect on n74245_1_pin13
  // NoConnect on n74245_1_pin14
  // NoConnect on n74245_1_pin6
  // NoConnect on n74245_1_pin5
  // NoConnect on n74245_1_pin15
  _74161 u_74161_2 (
    .pin1(n74161_2_pin1), .pin2(CLK), .pin3(AB[6]), .pin4(AB[5]), .pin5(AB[4]), .pin6(AB[3]),
    .pin7(n74161_1_pin10), .pin15(n74161_1_pin7), .pin14(n74161_2_pin14), .pin13(n74161_2_pin13),
    .pin12(n74161_2_pin12), .pin11(n74161_2_pin11), .pin10(n74161_2_pin10), .pin9(pull_resistor_1_node));
  _74245 u_74245_1 (
    .pin1(OE), .pin2(n74161_1_pin14), .pin3(n74161_1_pin13), .pin4(n74161_1_pin12), .pin5(n74245_1_pin5),
    .pin6(n74245_1_pin6), .pin7(n74245_1_pin7), .pin8(n74245_1_pin8), .pin9(n74245_1_pin9),
    .pin19(n74245_1_pin19), .pin18(AB[8]), .pin17(AB[9]), .pin16(AB[10]), .pin15(n74245_1_pin15),
    .pin14(n74245_1_pin14), .pin13(n74245_1_pin13), .pin12(n74245_1_pin12), .pin11(n74245_1_pin11));
  _74161 u_74161_3 (
    .pin1(n74161_3_pin1), .pin2(CLK), .pin3(AB[10]), .pin4(AB[9]), .pin5(AB[8]), .pin6(AB[7]), .pin7(CE),
    .pin15(n74161_1_pin10), .pin14(n74161_3_pin14), .pin13(n74161_3_pin13), .pin12(n74161_3_pin12),
    .pin11(n74161_3_pin11), .pin10(n74161_3_pin10), .pin9(pull_resistor_1_node));
  _74245 u_74245_2 (
    .pin1(OE), .pin2(n74161_3_pin14), .pin3(n74161_3_pin13), .pin4(n74161_3_pin12), .pin5(n74161_3_pin11),
    .pin6(n74161_2_pin14), .pin7(n74161_2_pin13), .pin8(n74161_2_pin12), .pin9(n74161_2_pin11),
    .pin19(n74245_2_pin19), .pin18(AB[0]), .pin17(AB[1]), .pin16(AB[2]), .pin15(AB[3]), .pin14(AB[4]),
    .pin13(AB[5]), .pin12(AB[6]), .pin11(AB[7]));
  // also tied to GND on the sheet: {n74245_1_pin19, n74245_2_pin19}
  // also tied to VCC on the sheet: {n74161_1_pin1, n74161_2_pin10, n74161_2_pin1, n74161_3_pin10, n74161_3_pin1}

  // Notes on the sheet:
  //   nor
endmodule

module at28c16 (
  input  I0,
  input  I1,
  input  I2,
  input  I3,
  input  I4,
  input  VCC,
  input  A10,
  input  A9,
  input  A8,
  input  A7,
  input  A6,
  input  A5,
  input  A4,
  input  A3,
  input  A2,
  input  A1,
  input  A0,
  input  I5,
  input  GND,
  input  I6,
  input  nCE,
  input  I7,
  input  nWE,
  input  nOE,
  output O0,
  output O1,
  output O2,
  output O3,
  output O4,
  output O5,
  output O6,
  output O7
);

  wire and_1_out, and_2_out, and_3_out, not_1_out, not_2_out, not_3_out, not_4_out, not_5_out;
  wire [7:0] ram_1_data;

  // NoConnect on VCC
  // NoConnect on GND
  not not_1 (not_1_out, nCE);
  not not_2 (not_2_out, nWE);
  not not_3 (not_3_out, nOE);
  and and_1 (and_1_out, not_1_out, not_2_out);
  not not_4 (not_4_out, and_2_out);
  and and_2 (and_2_out, not_1_out, not_3_out);
  and and_3 (and_3_out, and_1_out, not_4_out);
  RAM #(.addrWidth(11), .databus("bidir"), .trigger("high")) ram_1 (
    .addr({A10, A9, A8, A7, A6, A5, A4, A3, A2, A1, A0}), .we(and_3_out), .oe(not_3_out), .data(ram_1_data));
  assign ram_1_data = not_5_out ? {I7, I6, I5, I4, I3, I2, I1, I0} : 8'bz;  // Controlled_Buffer controlled_buffer_1
  not not_5 (not_5_out, and_2_out);
  assign {O7, O6, O5, O4, O3, O2, O1, O0} = and_2_out ? ram_1_data : 8'bz;  // Controlled_Buffer controlled_buffer_2
endmodule

module RX (
  input  VCC,
  input  [7:0] I,
  input  CLK,
  input  WE,
  input  OE,
  input  GND,
  output [7:0] O
);

  wire hc299_1_q0, hc299_1_q7, pull_resistor_1_node;
  wire [7:0] hc299_1_o0;

  Pull_Resistor #(.pull(1)) pull_resistor_1 (.node(pull_resistor_1_node));
  Transistor #(.\type ("n")) transistor_1 (.in(GND), .out(pull_resistor_1_node), .gate(OE));
  hc299 hc299_1 (
    .GND(GND), .S0(WE), .S1(WE), .VCC(VCC), .Dsl(GND), .Dsr(GND), .nOE1(pull_resistor_1_node),
    .nOE2(pull_resistor_1_node), .CP(CLK), .nMR(VCC), .I0(hc299_1_o0[0]), .I1(hc299_1_o0[1]),
    .I2(hc299_1_o0[2]), .I3(hc299_1_o0[3]), .I4(hc299_1_o0[4]), .I5(hc299_1_o0[5]), .I6(hc299_1_o0[6]),
    .I7(hc299_1_o0[7]), .Q7(hc299_1_q7), .Q0(hc299_1_q0), .O0(hc299_1_o0[0]), .O1(hc299_1_o0[1]),
    .O2(hc299_1_o0[2]), .O3(hc299_1_o0[3]), .O4(hc299_1_o0[4]), .O5(hc299_1_o0[5]), .O6(hc299_1_o0[6]),
    .O7(hc299_1_o0[7]));
  // NoConnect on hc299_1_q7
  // NoConnect on hc299_1_q0
  assign hc299_1_o0 = WE ? I : 8'bz;  // Controlled_Buffer controlled_buffer_1
  assign O = OE ? hc299_1_o0 : 8'bz;  // Controlled_Buffer controlled_buffer_2

  // Notes on the sheet:
  //   not
endmodule

module memory (
  input  VCC,
  input  CLK,
  input  WE,
  input  OE,
  input  [7:0] I,
  input  GND,
  input  [10:0] A,
  output [7:0] O
);

  wire and_1_out, nor_1_out, transistor_1_out, transistor_2_out;
  wire [7:0] at28c16_1_o0;

  at28c16 at28c16_1 (
    .A10(A[10]), .A9(A[9]), .A8(A[8]), .A7(A[7]), .A6(A[6]), .A5(A[5]), .A4(A[4]), .A3(A[3]), .A2(A[2]),
    .A1(A[1]), .A0(A[0]), .I2(at28c16_1_o0[2]), .I3(at28c16_1_o0[3]), .I4(at28c16_1_o0[4]),
    .I5(at28c16_1_o0[5]), .I6(at28c16_1_o0[6]), .I7(at28c16_1_o0[7]), .I0(at28c16_1_o0[0]),
    .I1(at28c16_1_o0[1]), .VCC(VCC), .GND(GND), .nCE(nor_1_out), .nWE(transistor_2_out),
    .nOE(transistor_1_out), .O0(at28c16_1_o0[0]), .O1(at28c16_1_o0[1]), .O2(at28c16_1_o0[2]),
    .O3(at28c16_1_o0[3]), .O4(at28c16_1_o0[4]), .O5(at28c16_1_o0[5]), .O6(at28c16_1_o0[6]),
    .O7(at28c16_1_o0[7]));
  Transistor #(.\type ("n")) transistor_1 (.in(GND), .out(transistor_1_out), .gate(OE));
  Transistor #(.\type ("n")) transistor_2 (.in(GND), .out(transistor_2_out), .gate(WE));
  Pull_Resistor #(.pull(1)) pull_resistor_1 (.node(transistor_1_out));
  Pull_Resistor #(.pull(1)) pull_resistor_2 (.node(transistor_2_out));
  and and_1 (and_1_out, WE, CLK);
  nor nor_1 (nor_1_out, OE, and_1_out);
  assign at28c16_1_o0 = WE ? I : 8'bz;  // Controlled_Buffer controlled_buffer_1
  assign O = OE ? at28c16_1_o0 : 8'bz;  // Controlled_Buffer controlled_buffer_2

  // Notes on the sheet:
  //   not
  //   Instead of the not gate after clk there should be pulse generator which wil generate brief pulse every time clk is set from 0 to 1
  //   Research this later
endmodule

module IR (
  input  [7:0] I,
  input  VCC,
  input  CLK,
  input  [2:0] IE,
  input  GND,
  output [23:0] COMMAND
);

  wire hc299_1_q0, hc299_1_q7, hc299_2_q0, hc299_2_q7, hc299_3_q0, hc299_3_q7, n74245_1_pin1,
       pull_resistor_1_node, pull_resistor_2_node, pull_resistor_3_node, pull_resistor_4_node,
       pull_resistor_5_node;

  Pull_Resistor #(.pull(1)) pull_resistor_1 (.node(pull_resistor_1_node));
  Transistor #(.\type ("n")) transistor_1 (.in(GND), .out(pull_resistor_1_node), .gate(IE[2]));
  Transistor #(.\type ("n")) transistor_2 (.in(GND), .out(pull_resistor_1_node), .gate(IE[1]));
  Transistor #(.\type ("n")) transistor_3 (.in(GND), .out(pull_resistor_1_node), .gate(IE[0]));
  Pull_Resistor #(.pull(1)) pull_resistor_2 (.node(pull_resistor_2_node));
  Transistor #(.\type ("n")) transistor_4 (.in(n74245_1_pin1), .out(pull_resistor_2_node), .gate(IE[0]));
  hc299 hc299_1 (
    .GND(GND), .S0(IE[0]), .S1(IE[0]), .VCC(VCC), .Dsl(GND), .Dsr(GND), .nOE1(pull_resistor_3_node),
    .nOE2(pull_resistor_3_node), .CP(CLK), .nMR(VCC), .I0(COMMAND[16]), .I1(COMMAND[17]), .I2(COMMAND[18]),
    .I3(COMMAND[19]), .I4(COMMAND[20]), .I5(COMMAND[21]), .I6(COMMAND[22]), .I7(COMMAND[23]),
    .Q7(hc299_1_q7), .Q0(hc299_1_q0), .O0(COMMAND[16]), .O1(COMMAND[17]), .O2(COMMAND[18]), .O3(COMMAND[19]),
    .O4(COMMAND[20]), .O5(COMMAND[21]), .O6(COMMAND[22]), .O7(COMMAND[23]));
  Pull_Resistor #(.pull(1)) pull_resistor_3 (.node(pull_resistor_3_node));
  Transistor #(.\type ("n")) transistor_5 (.in(GND), .out(pull_resistor_3_node), .gate(pull_resistor_1_node));
  _74245 u_74245_1 (
    .pin1(n74245_1_pin1), .pin2(COMMAND[23]), .pin3(COMMAND[22]), .pin4(COMMAND[21]), .pin5(COMMAND[20]),
    .pin6(COMMAND[19]), .pin7(COMMAND[18]), .pin8(COMMAND[17]), .pin9(COMMAND[16]),
    .pin19(pull_resistor_2_node), .pin18(I[7]), .pin17(I[6]), .pin16(I[5]), .pin15(I[4]), .pin14(I[3]),
    .pin13(I[2]), .pin12(I[1]), .pin11(I[0]));
  // NoConnect on hc299_1_q7
  // NoConnect on hc299_1_q0
  Pull_Resistor #(.pull(1)) pull_resistor_4 (.node(pull_resistor_4_node));
  Transistor #(.\type ("n")) transistor_6 (.in(n74245_1_pin1), .out(pull_resistor_4_node), .gate(IE[1]));
  hc299 hc299_2 (
    .GND(GND), .S0(IE[1]), .S1(IE[1]), .VCC(VCC), .Dsl(GND), .Dsr(GND), .nOE1(pull_resistor_3_node),
    .nOE2(pull_resistor_3_node), .CP(CLK), .nMR(VCC), .I0(COMMAND[8]), .I1(COMMAND[9]), .I2(COMMAND[10]),
    .I3(COMMAND[11]), .I4(COMMAND[12]), .I5(COMMAND[13]), .I6(COMMAND[14]), .I7(COMMAND[15]),
    .Q7(hc299_2_q7), .Q0(hc299_2_q0), .O0(COMMAND[8]), .O1(COMMAND[9]), .O2(COMMAND[10]), .O3(COMMAND[11]),
    .O4(COMMAND[12]), .O5(COMMAND[13]), .O6(COMMAND[14]), .O7(COMMAND[15]));
  _74245 u_74245_2 (
    .pin1(n74245_1_pin1), .pin2(COMMAND[15]), .pin3(COMMAND[14]), .pin4(COMMAND[13]), .pin5(COMMAND[12]),
    .pin6(COMMAND[11]), .pin7(COMMAND[10]), .pin8(COMMAND[9]), .pin9(COMMAND[8]),
    .pin19(pull_resistor_4_node), .pin18(I[7]), .pin17(I[6]), .pin16(I[5]), .pin15(I[4]), .pin14(I[3]),
    .pin13(I[2]), .pin12(I[1]), .pin11(I[0]));
  // NoConnect on hc299_2_q7
  // NoConnect on hc299_2_q0
  Pull_Resistor #(.pull(1)) pull_resistor_5 (.node(pull_resistor_5_node));
  Transistor #(.\type ("n")) transistor_7 (.in(n74245_1_pin1), .out(pull_resistor_5_node), .gate(IE[2]));
  _74245 u_74245_3 (
    .pin1(n74245_1_pin1), .pin2(COMMAND[7]), .pin3(COMMAND[6]), .pin4(COMMAND[5]), .pin5(COMMAND[4]),
    .pin6(COMMAND[3]), .pin7(COMMAND[2]), .pin8(COMMAND[1]), .pin9(COMMAND[0]), .pin19(pull_resistor_5_node),
    .pin18(I[7]), .pin17(I[6]), .pin16(I[5]), .pin15(I[4]), .pin14(I[3]), .pin13(I[2]), .pin12(I[1]),
    .pin11(I[0]));
  hc299 hc299_3 (
    .GND(GND), .S0(IE[2]), .S1(IE[2]), .VCC(VCC), .Dsl(GND), .Dsr(GND), .nOE1(pull_resistor_3_node),
    .nOE2(pull_resistor_3_node), .CP(CLK), .nMR(VCC), .I0(COMMAND[0]), .I1(COMMAND[1]), .I2(COMMAND[2]),
    .I3(COMMAND[3]), .I4(COMMAND[4]), .I5(COMMAND[5]), .I6(COMMAND[6]), .I7(COMMAND[7]), .Q7(hc299_3_q7),
    .Q0(hc299_3_q0), .O0(COMMAND[0]), .O1(COMMAND[1]), .O2(COMMAND[2]), .O3(COMMAND[3]), .O4(COMMAND[4]),
    .O5(COMMAND[5]), .O6(COMMAND[6]), .O7(COMMAND[7]));
  // NoConnect on hc299_3_q7
  // NoConnect on hc299_3_q0
  // also tied to GND on the sheet: n74245_1_pin1

  // Notes on the sheet:
  //   OR = NOR + NOT
  //   not
  //   nor
  //   not
  //   not
  //   not
endmodule

module registers (
  input  VCC,
  input  CLK,
  input  GND,
  input  [7:0] I,
  input  [2:0] A,
  input  WE,
  input  OE,
  output [7:0] O
);

  wire [7:0] controlled_buffer_2_out, n74138_1_pin15, n74138_2_pin15, pull_resistor_8_node,
       pull_resistor_16_node;

  assign O = OE ? controlled_buffer_2_out : 8'bz;  // Controlled_Buffer controlled_buffer_1
  assign controlled_buffer_2_out = WE ? I : 8'bz;  // Controlled_Buffer controlled_buffer_2
  Pull_Resistor #(.pull(1)) pull_resistor_1 (.node(pull_resistor_8_node[7]));
  Pull_Resistor #(.pull(1)) pull_resistor_2 (.node(pull_resistor_8_node[6]));
  Transistor #(.\type ("n")) transistor_1 (.in(GND), .out(pull_resistor_8_node[7]), .gate(n74138_1_pin15[7]));
  Transistor #(.\type ("n")) transistor_2 (.in(GND), .out(pull_resistor_8_node[6]), .gate(n74138_1_pin15[6]));
  Pull_Resistor #(.pull(1)) pull_resistor_3 (.node(pull_resistor_8_node[5]));
  Transistor #(.\type ("n")) transistor_3 (.in(GND), .out(pull_resistor_8_node[5]), .gate(n74138_1_pin15[5]));
  _74138 u_74138_1 (
    .pin1(A[0]), .pin2(A[1]), .pin3(A[2]), .pin4(GND), .pin5(GND), .pin6(WE), .pin7(n74138_1_pin15[7]),
    .pin15(n74138_1_pin15[0]), .pin14(n74138_1_pin15[1]), .pin13(n74138_1_pin15[2]),
    .pin12(n74138_1_pin15[3]), .pin11(n74138_1_pin15[4]), .pin10(n74138_1_pin15[5]), .pin9(n74138_1_pin15[6]));
  RX RX_7 (
    .CLK(CLK), .WE(pull_resistor_8_node[7]), .OE(pull_resistor_16_node[7]), .GND(GND), .VCC(VCC),
    .I(controlled_buffer_2_out), .O(controlled_buffer_2_out));
  Pull_Resistor #(.pull(1)) pull_resistor_4 (.node(pull_resistor_8_node[4]));
  Pull_Resistor #(.pull(1)) pull_resistor_5 (.node(pull_resistor_8_node[3]));
  Transistor #(.\type ("n")) transistor_4 (.in(GND), .out(pull_resistor_8_node[4]), .gate(n74138_1_pin15[4]));
  Transistor #(.\type ("n")) transistor_5 (.in(GND), .out(pull_resistor_8_node[3]), .gate(n74138_1_pin15[3]));
  Pull_Resistor #(.pull(1)) pull_resistor_6 (.node(pull_resistor_8_node[2]));
  Transistor #(.\type ("n")) transistor_6 (.in(GND), .out(pull_resistor_8_node[2]), .gate(n74138_1_pin15[2]));
  Transistor #(.\type ("n")) transistor_7 (.in(GND), .out(pull_resistor_8_node[1]), .gate(n74138_1_pin15[1]));
  Pull_Resistor #(.pull(1)) pull_resistor_7 (.node(pull_resistor_8_node[1]));
  Pull_Resistor #(.pull(1)) pull_resistor_8 (.node(pull_resistor_8_node[0]));
  Transistor #(.\type ("n")) transistor_8 (.in(GND), .out(pull_resistor_8_node[0]), .gate(n74138_1_pin15[0]));
  RX RX_6 (
    .CLK(CLK), .WE(pull_resistor_8_node[6]), .OE(pull_resistor_16_node[6]), .GND(GND), .VCC(VCC),
    .I(controlled_buffer_2_out), .O(controlled_buffer_2_out));
  Pull_Resistor #(.pull(1)) pull_resistor_9 (.node(pull_resistor_16_node[7]));
  Pull_Resistor #(.pull(1)) pull_resistor_10 (.node(pull_resistor_16_node[6]));
  Transistor #(.\type ("n")) transistor_9 (.in(GND), .out(pull_resistor_16_node[7]), .gate(n74138_2_pin15[7]));
  Transistor #(.\type ("n")) transistor_10 (.in(GND), .out(pull_resistor_16_node[6]), .gate(n74138_2_pin15[6]));
  Pull_Resistor #(.pull(1)) pull_resistor_11 (.node(pull_resistor_16_node[5]));
  Transistor #(.\type ("n")) transistor_11 (.in(GND), .out(pull_resistor_16_node[5]), .gate(n74138_2_pin15[5]));
  _74138 u_74138_2 (
    .pin1(A[0]), .pin2(A[1]), .pin3(A[2]), .pin4(GND), .pin5(GND), .pin6(OE), .pin7(n74138_2_pin15[7]),
    .pin15(n74138_2_pin15[0]), .pin14(n74138_2_pin15[1]), .pin13(n74138_2_pin15[2]),
    .pin12(n74138_2_pin15[3]), .pin11(n74138_2_pin15[4]), .pin10(n74138_2_pin15[5]), .pin9(n74138_2_pin15[6]));
  RX RX_5 (
    .CLK(CLK), .WE(pull_resistor_8_node[5]), .OE(pull_resistor_16_node[5]), .GND(GND), .VCC(VCC),
    .I(controlled_buffer_2_out), .O(controlled_buffer_2_out));
  Pull_Resistor #(.pull(1)) pull_resistor_12 (.node(pull_resistor_16_node[4]));
  Pull_Resistor #(.pull(1)) pull_resistor_13 (.node(pull_resistor_16_node[3]));
  Transistor #(.\type ("n")) transistor_12 (.in(GND), .out(pull_resistor_16_node[4]), .gate(n74138_2_pin15[4]));
  Transistor #(.\type ("n")) transistor_13 (.in(GND), .out(pull_resistor_16_node[3]), .gate(n74138_2_pin15[3]));
  Pull_Resistor #(.pull(1)) pull_resistor_14 (.node(pull_resistor_16_node[2]));
  Transistor #(.\type ("n")) transistor_14 (.in(GND), .out(pull_resistor_16_node[2]), .gate(n74138_2_pin15[2]));
  Transistor #(.\type ("n")) transistor_15 (.in(GND), .out(pull_resistor_16_node[1]), .gate(n74138_2_pin15[1]));
  Pull_Resistor #(.pull(1)) pull_resistor_15 (.node(pull_resistor_16_node[1]));
  Pull_Resistor #(.pull(1)) pull_resistor_16 (.node(pull_resistor_16_node[0]));
  Transistor #(.\type ("n")) transistor_16 (.in(GND), .out(pull_resistor_16_node[0]), .gate(n74138_2_pin15[0]));
  RX RX_4 (
    .CLK(CLK), .WE(pull_resistor_8_node[4]), .OE(pull_resistor_16_node[4]), .GND(GND), .VCC(VCC),
    .I(controlled_buffer_2_out), .O(controlled_buffer_2_out));
  RX RX_3 (
    .CLK(CLK), .WE(pull_resistor_8_node[3]), .OE(pull_resistor_16_node[3]), .GND(GND), .VCC(VCC),
    .I(controlled_buffer_2_out), .O(controlled_buffer_2_out));
  RX RX_2 (
    .CLK(CLK), .WE(pull_resistor_8_node[2]), .OE(pull_resistor_16_node[2]), .GND(GND), .VCC(VCC),
    .I(controlled_buffer_2_out), .O(controlled_buffer_2_out));
  RX RX_1 (
    .CLK(CLK), .WE(pull_resistor_8_node[1]), .OE(pull_resistor_16_node[1]), .GND(GND), .VCC(VCC),
    .I(controlled_buffer_2_out), .O(controlled_buffer_2_out));
  RX RX_0 (
    .CLK(CLK), .WE(pull_resistor_8_node[0]), .OE(pull_resistor_16_node[0]), .GND(GND), .VCC(VCC),
    .I(controlled_buffer_2_out), .O(controlled_buffer_2_out));
endmodule

module core (
  input  VCC,
  input  CLK,
  input  GND,
  input  [15:0] CB,
  input  [23:0] IR_CMD,
  input  CR_EMP,
  input  [4:0] ALU_STATE,
  output SG_CLR,
  output [2:0] IR_IE,
  output IP_CE,
  output [10:0] A,
  output HLT,
  output IP_WE,
  output IP_OE,
  output MEM_WE,
  output MEM_OE,
  output CR_WE,
  output CR_OE,
  output CR_CE,
  output REGS_WE,
  output REGS_OE,
  output [2:0] REGS_A,
  output [1:0] ALU_MODE,
  output [2:0] ALU_OPSEL,
  output ALU_EN,
  output BR_WE,
  output BR_OE
);

  or or_1 (IP_CE, CB[4], CB[2], CB[0]);

  assign IR_IE = {CB[5], CB[3], CB[1]};
  assign SG_CLR = CB[7];
endmodule

module clock_generator (
  input  VCC,
  input  GND,
  input  HLT,
  output CLK
);

  wire clock_1_out, not_1_out;

  // NoConnect on VCC
  // NoConnect on GND
  not not_1 (not_1_out, HLT);
  Clock clock_1 (.out(clock_1_out));
  and and_1 (CLK, not_1_out, clock_1_out);
endmodule

module voltage_source (
  input  ON_OFF,
  output VCC,
  output GND
);

  assign VCC = ON_OFF ? 1'b1 : 1'bz;  // Controlled_Buffer controlled_buffer_1

  assign GND = 1'b0;
endmodule

module hc154en (
  input  VCC,
  input  GND,
  input  A0,
  input  A1,
  input  A2,
  input  A3,
  input  nE0,
  input  nE1,
  output nY0,
  output nY1,
  output nY2,
  output nY3,
  output nY4,
  output nY5,
  output nY6,
  output nY7,
  output nY8,
  output nY9,
  output nY10,
  output nY11,
  output nY12,
  output nY13,
  output nY14,
  output nY15
);

  wire and_1_out, and_2_out, not_1_out, not_2_out, not_3_out, not_4_out, not_5_out, not_6_out, not_7_out,
       not_8_out, not_9_out, not_10_out, not_11_out, not_12_out, not_13_out, not_14_out, not_15_out,
       not_16_out, not_17_out, or_1_out, or_2_out, or_3_out, or_4_out, or_5_out, or_6_out, or_7_out,
       or_8_out, or_9_out, or_10_out, or_11_out, or_12_out, or_13_out, or_14_out, or_15_out, or_16_out;
  wire [15:0] decoder_1_out0;

  and and_1 (and_1_out, VCC, not_1_out);
  not not_1 (not_1_out, GND);
  Decoder #(.enable("false"), .select(4)) decoder_1 (
    .out0(decoder_1_out0[0]), .out1(decoder_1_out0[1]), .out2(decoder_1_out0[2]), .out3(decoder_1_out0[3]),
    .out4(decoder_1_out0[4]), .out5(decoder_1_out0[5]), .out6(decoder_1_out0[6]), .out7(decoder_1_out0[7]),
    .out8(decoder_1_out0[8]), .out9(decoder_1_out0[9]), .out10(decoder_1_out0[10]),
    .out11(decoder_1_out0[11]), .out12(decoder_1_out0[12]), .out13(decoder_1_out0[13]),
    .out14(decoder_1_out0[14]), .out15(decoder_1_out0[15]), .sel({A3, A2, A1, A0}));
  and and_2 (and_2_out, nE0, nE1);
  not not_2 (not_2_out, decoder_1_out0[0]);
  not not_3 (not_3_out, decoder_1_out0[1]);
  not not_4 (not_4_out, decoder_1_out0[2]);
  not not_5 (not_5_out, decoder_1_out0[3]);
  not not_6 (not_6_out, decoder_1_out0[4]);
  not not_7 (not_7_out, decoder_1_out0[5]);
  not not_8 (not_8_out, decoder_1_out0[6]);
  not not_9 (not_9_out, decoder_1_out0[7]);
  not not_10 (not_10_out, decoder_1_out0[8]);
  not not_11 (not_11_out, decoder_1_out0[9]);
  not not_12 (not_12_out, decoder_1_out0[10]);
  not not_13 (not_13_out, decoder_1_out0[11]);
  not not_14 (not_14_out, decoder_1_out0[12]);
  not not_15 (not_15_out, decoder_1_out0[13]);
  not not_16 (not_16_out, decoder_1_out0[14]);
  not not_17 (not_17_out, decoder_1_out0[15]);
  or or_1 (or_1_out, not_2_out, and_2_out);
  assign nY0 = and_1_out ? or_1_out : 1'bz;  // Controlled_Buffer controlled_buffer_1
  or or_2 (or_2_out, not_3_out, and_2_out);
  assign nY1 = and_1_out ? or_2_out : 1'bz;  // Controlled_Buffer controlled_buffer_2
  or or_3 (or_3_out, not_4_out, and_2_out);
  assign nY2 = and_1_out ? or_3_out : 1'bz;  // Controlled_Buffer controlled_buffer_3
  or or_4 (or_4_out, not_5_out, and_2_out);
  assign nY3 = and_1_out ? or_4_out : 1'bz;  // Controlled_Buffer controlled_buffer_4
  or or_5 (or_5_out, not_6_out, and_2_out);
  assign nY4 = and_1_out ? or_5_out : 1'bz;  // Controlled_Buffer controlled_buffer_5
  or or_6 (or_6_out, not_7_out, and_2_out);
  assign nY5 = and_1_out ? or_6_out : 1'bz;  // Controlled_Buffer controlled_buffer_6
  or or_7 (or_7_out, not_8_out, and_2_out);
  assign nY6 = and_1_out ? or_7_out : 1'bz;  // Controlled_Buffer controlled_buffer_7
  or or_8 (or_8_out, not_9_out, and_2_out);
  assign nY7 = and_1_out ? or_8_out : 1'bz;  // Controlled_Buffer controlled_buffer_8
  or or_9 (or_9_out, not_10_out, and_2_out);
  assign nY8 = and_1_out ? or_9_out : 1'bz;  // Controlled_Buffer controlled_buffer_9
  or or_10 (or_10_out, not_11_out, and_2_out);
  assign nY9 = and_1_out ? or_10_out : 1'bz;  // Controlled_Buffer controlled_buffer_10
  or or_11 (or_11_out, not_12_out, and_2_out);
  assign nY10 = and_1_out ? or_11_out : 1'bz;  // Controlled_Buffer controlled_buffer_11
  or or_12 (or_12_out, not_13_out, and_2_out);
  assign nY11 = and_1_out ? or_12_out : 1'bz;  // Controlled_Buffer controlled_buffer_12
  or or_13 (or_13_out, not_14_out, and_2_out);
  assign nY12 = and_1_out ? or_13_out : 1'bz;  // Controlled_Buffer controlled_buffer_13
  or or_14 (or_14_out, not_15_out, and_2_out);
  assign nY13 = and_1_out ? or_14_out : 1'bz;  // Controlled_Buffer controlled_buffer_14
  or or_15 (or_15_out, not_16_out, and_2_out);
  assign nY14 = and_1_out ? or_15_out : 1'bz;  // Controlled_Buffer controlled_buffer_15
  or or_16 (or_16_out, not_17_out, and_2_out);
  assign nY15 = and_1_out ? or_16_out : 1'bz;  // Controlled_Buffer controlled_buffer_16
endmodule

module CR (
  input  [7:0] I,
  input  WE,
  input  VCC,
  input  CLK,
  input  CE,
  input  OE,
  input  GND,
  output EMP,
  output [7:0] O
);

  wire and_2_out, n74193_1_pin4, n74193_1_pin11, n74193_1_pin12, n74193_1_pin13, n74193_2_pin4,
       n74193_2_pin12, n74245_1_pin19, not_3_out;
  wire [7:0] n74245_1_pin11;

  _74193 #(.VccGndPorts("true")) u_74193_1 (
    .pin1(I[5]), .pin2(n74245_1_pin11[5]), .pin3(n74245_1_pin11[4]), .pin4(n74193_1_pin4), .pin5(VCC),
    .pin6(n74245_1_pin11[6]), .pin7(n74245_1_pin11[7]), .pin8(GND), .pin16(VCC), .pin15(I[4]), .pin14(GND),
    .pin13(n74193_1_pin13), .pin12(n74193_1_pin12), .pin11(n74193_1_pin11), .pin10(I[6]), .pin9(I[7]));
  // NoConnect on n74193_1_pin13
  // NoConnect on n74193_1_pin12
  _74245 u_74245_1 (
    .pin1(GND), .pin2(O[7]), .pin3(O[6]), .pin4(O[5]), .pin5(O[4]), .pin6(O[3]), .pin7(O[2]), .pin8(O[1]),
    .pin9(O[0]), .pin19(n74245_1_pin19), .pin18(n74245_1_pin11[7]), .pin17(n74245_1_pin11[6]),
    .pin16(n74245_1_pin11[5]), .pin15(n74245_1_pin11[4]), .pin14(n74245_1_pin11[3]),
    .pin13(n74245_1_pin11[2]), .pin12(n74245_1_pin11[1]), .pin11(n74245_1_pin11[0]));
  not not_1 (n74245_1_pin19, OE);
  _74193 #(.VccGndPorts("true")) u_74193_2 (
    .pin1(I[1]), .pin2(n74245_1_pin11[1]), .pin3(n74245_1_pin11[0]), .pin4(n74193_2_pin4), .pin5(VCC),
    .pin6(n74245_1_pin11[2]), .pin7(n74245_1_pin11[3]), .pin8(GND), .pin16(VCC), .pin15(I[0]), .pin14(GND),
    .pin13(n74193_1_pin4), .pin12(n74193_2_pin12), .pin11(n74193_1_pin11), .pin10(I[2]), .pin9(I[3]));
  // NoConnect on n74193_2_pin12
  and and_1 (n74193_2_pin4, CLK, CE, not_3_out);
  nor nor_1 (EMP, n74245_1_pin11[0], n74245_1_pin11[1], n74245_1_pin11[2], n74245_1_pin11[3], n74245_1_pin11[4], n74245_1_pin11[5], n74245_1_pin11[6], n74245_1_pin11[7]);
  and and_2 (and_2_out, WE, CLK);
  not not_2 (n74193_1_pin11, and_2_out);
  not not_3 (not_3_out, EMP);

  // Notes on the sheet:
  //   ADD PULSE GENERATOR FOR ASYNC LOAD!!!
  //   I leave this with logic gates to not be confused later
endmodule

module ALU (
  input  GND,
  input  CLK,
  input  VCC,
  input  [7:0] I,
  input  EN,
  input  [1:0] MODE,
  input  [2:0] OPSEL,
  output [7:0] O,
  output [4:0] STATE
);

  wire A_q0, A_q7, and_1_out, and_2_out, and_3_out, and_4_out, and_5_out, B_q0, B_q7, n7485_1_pin2,
       n7485_1_pin3, n7485_1_pin4, n7485_1_pin5, n7485_1_pin6, n7485_1_pin7, n7485_2_pin2, n7485_2_pin3,
       n7485_2_pin4, n7486_2_pin3, n7486_2_pin6, n7486_2_pin8, n7486_2_pin11, n74138_1_pin6, n74138_1_pin7,
       n74138_1_pin9, n74138_1_pin10, n74138_1_pin11, n74138_1_pin12, n74138_1_pin13, n74138_1_pin14,
       n74138_1_pin15, n74245_1_pin1, n74245_2_pin1, n74245_4_pin1, n74245_5_pin1, n74245_6_pin1,
       n74245_7_pin1, n74245_8_pin1, n74283_1_pin2, n74283_1_pin6, n74283_1_pin7, n74283_1_pin9,
       n74283_1_pin11, n74283_1_pin15, nor_1_out, not_1_out, not_2_out, not_3_out, not_4_out, not_5_out,
       not_6_out, not_7_out, not_8_out, or_1_out;
  wire [7:0] n7486_2_pin10, n74245_1_pin9, n74245_1_pin11, n74245_5_pin11, n74245_6_pin11, n74245_7_pin11,
       n74245_8_pin11, n74283_2_pin5;

  and and_1 (and_1_out, EN, CLK);
  LED led_1 (.in(n74283_1_pin9));
  and and_2 (and_2_out, n74138_1_pin7, n74138_1_pin9);
  or or_1 (or_1_out, MODE[0], MODE[1]);
  not not_1 (not_1_out, EN);
  _74283 #(.ShowInternalStructure("true")) u_74283_1 (
    .pin1(n74245_1_pin11[5]), .pin2(n74283_1_pin2), .pin3(n74283_2_pin5[5]), .pin4(n74245_1_pin11[4]),
    .pin5(n74283_2_pin5[4]), .pin6(n74283_1_pin6), .pin7(n74283_1_pin7), .pin15(n74283_1_pin15),
    .pin14(n74283_2_pin5[6]), .pin13(n74245_1_pin11[6]), .pin12(n74283_2_pin5[7]), .pin11(n74283_1_pin11),
    .pin10(n74245_1_pin11[7]), .pin9(n74283_1_pin9));
  _74245 u_74245_1 (
    .pin1(n74245_1_pin1), .pin2(n74245_1_pin9[7]), .pin3(n74245_1_pin9[6]), .pin4(n74245_1_pin9[5]),
    .pin5(n74245_1_pin9[4]), .pin6(n74245_1_pin9[3]), .pin7(n74245_1_pin9[2]), .pin8(n74245_1_pin9[1]),
    .pin9(n74245_1_pin9[0]), .pin19(and_2_out), .pin18(n74245_1_pin11[7]), .pin17(n74245_1_pin11[6]),
    .pin16(n74245_1_pin11[5]), .pin15(n74245_1_pin11[4]), .pin14(n74245_1_pin11[3]),
    .pin13(n74245_1_pin11[2]), .pin12(n74245_1_pin11[1]), .pin11(n74245_1_pin11[0]));
  not not_2 (not_2_out, OPSEL[2]);
  not not_3 (not_3_out, OPSEL[1]);
  not not_4 (not_4_out, OPSEL[0]);
  _74138 u_74138_1 (
    .pin1(not_4_out), .pin2(not_3_out), .pin3(not_2_out), .pin4(or_1_out), .pin5(not_1_out),
    .pin6(n74138_1_pin6), .pin7(n74138_1_pin7), .pin15(n74138_1_pin15), .pin14(n74138_1_pin14),
    .pin13(n74138_1_pin13), .pin12(n74138_1_pin12), .pin11(n74138_1_pin11), .pin10(n74138_1_pin10),
    .pin9(n74138_1_pin9));
  and and_3 (and_3_out, n74138_1_pin15, n74138_1_pin10);
  _7486 #(.ShowInternalStructure("true")) u_7486_1 (
    .pin1(n7486_2_pin10[7]), .pin2(n74138_1_pin7), .pin3(n74283_1_pin11), .pin4(n7486_2_pin10[5]),
    .pin5(n74138_1_pin7), .pin6(n74283_1_pin2), .pin13(n7486_2_pin10[6]), .pin12(n74138_1_pin7),
    .pin11(n74283_1_pin15), .pin10(n7486_2_pin10[4]), .pin9(n74138_1_pin7), .pin8(n74283_1_pin6));
  _7486 #(.ShowInternalStructure("true")) u_7486_2 (
    .pin1(n7486_2_pin10[3]), .pin2(n74138_1_pin7), .pin3(n7486_2_pin3), .pin4(n7486_2_pin10[1]),
    .pin5(n74138_1_pin7), .pin6(n7486_2_pin6), .pin13(n7486_2_pin10[2]), .pin12(n74138_1_pin7),
    .pin11(n7486_2_pin11), .pin10(n7486_2_pin10[0]), .pin9(n74138_1_pin7), .pin8(n7486_2_pin8));
  _74283 #(.ShowInternalStructure("true")) u_74283_2 (
    .pin1(n74245_1_pin11[1]), .pin2(n7486_2_pin6), .pin3(n74283_2_pin5[1]), .pin4(n74245_1_pin11[0]),
    .pin5(n74283_2_pin5[0]), .pin6(n7486_2_pin8), .pin7(n74138_1_pin7), .pin15(n7486_2_pin11),
    .pin14(n74283_2_pin5[2]), .pin13(n74245_1_pin11[2]), .pin12(n74283_2_pin5[3]), .pin11(n7486_2_pin3),
    .pin10(n74245_1_pin11[3]), .pin9(n74283_1_pin7));
  not not_5 (not_5_out, MODE[0]);
  _74245 u_74245_2 (
    .pin1(n74245_2_pin1), .pin2(n74283_2_pin5[7]), .pin3(n74283_2_pin5[6]), .pin4(n74283_2_pin5[5]),
    .pin5(n74283_2_pin5[4]), .pin6(n74283_2_pin5[3]), .pin7(n74283_2_pin5[2]), .pin8(n74283_2_pin5[1]),
    .pin9(n74283_2_pin5[0]), .pin19(not_5_out), .pin18(n74245_1_pin9[7]), .pin17(n74245_1_pin9[6]),
    .pin16(n74245_1_pin9[5]), .pin15(n74245_1_pin9[4]), .pin14(n74245_1_pin9[3]), .pin13(n74245_1_pin9[2]),
    .pin12(n74245_1_pin9[1]), .pin11(n74245_1_pin9[0]));
  hc299 A (
    .GND(1'b0), .S0(MODE[0]), .S1(MODE[0]), .VCC(1'b1), .Dsl(1'b0), .Dsr(1'b0), .nOE1(MODE[0]),
    .nOE2(MODE[0]), .CP(and_1_out), .nMR(1'b1), .I0(n74283_2_pin5[0]), .I1(n74283_2_pin5[1]),
    .I2(n74283_2_pin5[2]), .I3(n74283_2_pin5[3]), .I4(n74283_2_pin5[4]), .I5(n74283_2_pin5[5]),
    .I6(n74283_2_pin5[6]), .I7(n74283_2_pin5[7]), .Q7(A_q7), .Q0(A_q0), .O0(n74283_2_pin5[0]),
    .O1(n74283_2_pin5[1]), .O2(n74283_2_pin5[2]), .O3(n74283_2_pin5[3]), .O4(n74283_2_pin5[4]),
    .O5(n74283_2_pin5[5]), .O6(n74283_2_pin5[6]), .O7(n74283_2_pin5[7]));
  nor nor_1 (nor_1_out, MODE[1], MODE[0]);
  // NoConnect on A_q7
  not not_6 (not_6_out, EN);
  _74245 u_74245_3 (
    .pin1(nor_1_out), .pin2(n74245_1_pin9[7]), .pin3(n74245_1_pin9[6]), .pin4(n74245_1_pin9[5]),
    .pin5(n74245_1_pin9[4]), .pin6(n74245_1_pin9[3]), .pin7(n74245_1_pin9[2]), .pin8(n74245_1_pin9[1]),
    .pin9(n74245_1_pin9[0]), .pin19(not_6_out), .pin18(I[7]), .pin17(I[6]), .pin16(I[5]), .pin15(I[4]),
    .pin14(I[3]), .pin13(I[2]), .pin12(I[1]), .pin11(I[0]));
  // NoConnect on A_q0
  and and_4 (and_4_out, and_1_out, not_8_out);
  or or_2 (STATE[3], STATE[4], STATE[2]);
  not not_7 (not_7_out, MODE[1]);
  _74245 u_74245_4 (
    .pin1(n74245_4_pin1), .pin2(n7486_2_pin10[7]), .pin3(n7486_2_pin10[6]), .pin4(n7486_2_pin10[5]),
    .pin5(n7486_2_pin10[4]), .pin6(n7486_2_pin10[3]), .pin7(n7486_2_pin10[2]), .pin8(n7486_2_pin10[1]),
    .pin9(n7486_2_pin10[0]), .pin19(not_7_out), .pin18(n74245_1_pin9[7]), .pin17(n74245_1_pin9[6]),
    .pin16(n74245_1_pin9[5]), .pin15(n74245_1_pin9[4]), .pin14(n74245_1_pin9[3]), .pin13(n74245_1_pin9[2]),
    .pin12(n74245_1_pin9[1]), .pin11(n74245_1_pin9[0]));
  // NoConnect on B_q7
  hc299 B (
    .GND(1'b0), .S0(MODE[1]), .S1(MODE[1]), .VCC(1'b1), .Dsl(1'b0), .Dsr(1'b0), .nOE1(MODE[1]),
    .nOE2(MODE[1]), .CP(and_1_out), .nMR(1'b1), .I0(n7486_2_pin10[0]), .I1(n7486_2_pin10[1]),
    .I2(n7486_2_pin10[2]), .I3(n7486_2_pin10[3]), .I4(n7486_2_pin10[4]), .I5(n7486_2_pin10[5]),
    .I6(n7486_2_pin10[6]), .I7(n7486_2_pin10[7]), .Q7(B_q7), .Q0(B_q0), .O0(n7486_2_pin10[0]),
    .O1(n7486_2_pin10[1]), .O2(n7486_2_pin10[2]), .O3(n7486_2_pin10[3]), .O4(n7486_2_pin10[4]),
    .O5(n7486_2_pin10[5]), .O6(n7486_2_pin10[6]), .O7(n7486_2_pin10[7]));
  _7485 #(.ShowInternalStructure("true")) u_7485_1 (
    .pin1(n7486_2_pin10[7]), .pin2(n7485_1_pin2), .pin3(n7485_1_pin3), .pin4(n7485_1_pin4),
    .pin5(n7485_1_pin5), .pin6(n7485_1_pin6), .pin7(n7485_1_pin7), .pin15(n74283_2_pin5[7]),
    .pin14(n7486_2_pin10[6]), .pin13(n74283_2_pin5[6]), .pin12(n74283_2_pin5[5]), .pin11(n7486_2_pin10[5]),
    .pin10(n74283_2_pin5[4]), .pin9(n7486_2_pin10[4]));
  not not_8 (not_8_out, n74138_1_pin10);
  _74175 #(.ShowInternalStructure("true")) u_74175_1 (
    .pin2(STATE[0]), .pin4(n7485_1_pin7), .pin5(n7485_1_pin6), .pin7(STATE[2]), .pin12(n7485_1_pin5),
    .pin10(STATE[4]), .pin9(and_4_out));  // open: pin1, pin3, pin6, pin15, pin14, pin13, pin11
  or or_3 (STATE[1], STATE[2], STATE[0]);
  and and_5 (and_5_out, EN, and_3_out, nor_1_out);
  // NoConnect on B_q0
  assign O = and_5_out ? n74245_1_pin9 : 8'bz;  // Controlled_Buffer controlled_buffer_1
  _7485 #(.ShowInternalStructure("true")) u_7485_2 (
    .pin1(n7486_2_pin10[3]), .pin2(n7485_2_pin2), .pin3(n7485_2_pin3), .pin4(n7485_2_pin4),
    .pin5(n7485_1_pin4), .pin6(n7485_1_pin3), .pin7(n7485_1_pin2), .pin15(n74283_2_pin5[3]),
    .pin14(n7486_2_pin10[2]), .pin13(n74283_2_pin5[2]), .pin12(n74283_2_pin5[1]), .pin11(n7486_2_pin10[1]),
    .pin10(n74283_2_pin5[0]), .pin9(n7486_2_pin10[0]));
  _7486 #(.ShowInternalStructure("true")) u_7486_3 (
    .pin1(n74283_2_pin5[7]), .pin2(n7486_2_pin10[7]), .pin3(n74245_5_pin11[7]), .pin4(n74283_2_pin5[5]),
    .pin5(n7486_2_pin10[5]), .pin6(n74245_5_pin11[5]), .pin13(n74283_2_pin5[6]), .pin12(n7486_2_pin10[6]),
    .pin11(n74245_5_pin11[6]), .pin10(n74283_2_pin5[4]), .pin9(n7486_2_pin10[4]), .pin8(n74245_5_pin11[4]));
  _74245 u_74245_5 (
    .pin1(n74245_5_pin1), .pin2(n74245_1_pin9[7]), .pin3(n74245_1_pin9[6]), .pin4(n74245_1_pin9[5]),
    .pin5(n74245_1_pin9[4]), .pin6(n74245_1_pin9[3]), .pin7(n74245_1_pin9[2]), .pin8(n74245_1_pin9[1]),
    .pin9(n74245_1_pin9[0]), .pin19(n74138_1_pin11), .pin18(n74245_5_pin11[7]), .pin17(n74245_5_pin11[6]),
    .pin16(n74245_5_pin11[5]), .pin15(n74245_5_pin11[4]), .pin14(n74245_5_pin11[3]),
    .pin13(n74245_5_pin11[2]), .pin12(n74245_5_pin11[1]), .pin11(n74245_5_pin11[0]));
  _7486 #(.ShowInternalStructure("true")) u_7486_4 (
    .pin1(n74283_2_pin5[3]), .pin2(n7486_2_pin10[3]), .pin3(n74245_5_pin11[3]), .pin4(n74283_2_pin5[1]),
    .pin5(n7486_2_pin10[1]), .pin6(n74245_5_pin11[1]), .pin13(n74283_2_pin5[2]), .pin12(n7486_2_pin10[2]),
    .pin11(n74245_5_pin11[2]), .pin10(n74283_2_pin5[0]), .pin9(n7486_2_pin10[0]), .pin8(n74245_5_pin11[0]));
  _7408 #(.ShowInternalStructure("true")) u_7408_1 (
    .pin1(n74283_2_pin5[7]), .pin2(n7486_2_pin10[7]), .pin3(n74245_6_pin11[7]), .pin4(n74283_2_pin5[5]),
    .pin5(n7486_2_pin10[5]), .pin6(n74245_6_pin11[5]), .pin13(n74283_2_pin5[6]), .pin12(n7486_2_pin10[6]),
    .pin11(n74245_6_pin11[6]), .pin10(n74283_2_pin5[4]), .pin9(n7486_2_pin10[4]), .pin8(n74245_6_pin11[4]));
  _74245 u_74245_6 (
    .pin1(n74245_6_pin1), .pin2(n74245_1_pin9[7]), .pin3(n74245_1_pin9[6]), .pin4(n74245_1_pin9[5]),
    .pin5(n74245_1_pin9[4]), .pin6(n74245_1_pin9[3]), .pin7(n74245_1_pin9[2]), .pin8(n74245_1_pin9[1]),
    .pin9(n74245_1_pin9[0]), .pin19(n74138_1_pin12), .pin18(n74245_6_pin11[7]), .pin17(n74245_6_pin11[6]),
    .pin16(n74245_6_pin11[5]), .pin15(n74245_6_pin11[4]), .pin14(n74245_6_pin11[3]),
    .pin13(n74245_6_pin11[2]), .pin12(n74245_6_pin11[1]), .pin11(n74245_6_pin11[0]));
  _7408 #(.ShowInternalStructure("true")) u_7408_2 (
    .pin1(n74283_2_pin5[3]), .pin2(n7486_2_pin10[3]), .pin3(n74245_6_pin11[3]), .pin4(n74283_2_pin5[1]),
    .pin5(n7486_2_pin10[1]), .pin6(n74245_6_pin11[1]), .pin13(n74283_2_pin5[2]), .pin12(n7486_2_pin10[2]),
    .pin11(n74245_6_pin11[2]), .pin10(n74283_2_pin5[0]), .pin9(n7486_2_pin10[0]), .pin8(n74245_6_pin11[0]));
  _7432 #(.ShowInternalStructure("true")) u_7432_1 (
    .pin1(n74283_2_pin5[7]), .pin2(n7486_2_pin10[7]), .pin3(n74245_7_pin11[7]), .pin4(n74283_2_pin5[5]),
    .pin5(n7486_2_pin10[5]), .pin6(n74245_7_pin11[5]), .pin13(n74283_2_pin5[6]), .pin12(n7486_2_pin10[6]),
    .pin11(n74245_7_pin11[6]), .pin10(n74283_2_pin5[4]), .pin9(n7486_2_pin10[4]), .pin8(n74245_7_pin11[4]));
  _74245 u_74245_7 (
    .pin1(n74245_7_pin1), .pin2(n74245_1_pin9[7]), .pin3(n74245_1_pin9[6]), .pin4(n74245_1_pin9[5]),
    .pin5(n74245_1_pin9[4]), .pin6(n74245_1_pin9[3]), .pin7(n74245_1_pin9[2]), .pin8(n74245_1_pin9[1]),
    .pin9(n74245_1_pin9[0]), .pin19(n74138_1_pin13), .pin18(n74245_7_pin11[7]), .pin17(n74245_7_pin11[6]),
    .pin16(n74245_7_pin11[5]), .pin15(n74245_7_pin11[4]), .pin14(n74245_7_pin11[3]),
    .pin13(n74245_7_pin11[2]), .pin12(n74245_7_pin11[1]), .pin11(n74245_7_pin11[0]));
  _7432 #(.ShowInternalStructure("true")) u_7432_2 (
    .pin1(n74283_2_pin5[3]), .pin2(n7486_2_pin10[3]), .pin3(n74245_7_pin11[3]), .pin4(n74283_2_pin5[1]),
    .pin5(n7486_2_pin10[1]), .pin6(n74245_7_pin11[1]), .pin13(n74283_2_pin5[2]), .pin12(n7486_2_pin10[2]),
    .pin11(n74245_7_pin11[2]), .pin10(n74283_2_pin5[0]), .pin9(n7486_2_pin10[0]), .pin8(n74245_7_pin11[0]));
  _74245 u_74245_8 (
    .pin1(n74245_8_pin1), .pin2(n74245_1_pin9[7]), .pin3(n74245_1_pin9[6]), .pin4(n74245_1_pin9[5]),
    .pin5(n74245_1_pin9[4]), .pin6(n74245_1_pin9[3]), .pin7(n74245_1_pin9[2]), .pin8(n74245_1_pin9[1]),
    .pin9(n74245_1_pin9[0]), .pin19(n74138_1_pin14), .pin18(n74245_8_pin11[7]), .pin17(n74245_8_pin11[6]),
    .pin16(n74245_8_pin11[5]), .pin15(n74245_8_pin11[4]), .pin14(n74245_8_pin11[3]),
    .pin13(n74245_8_pin11[2]), .pin12(n74245_8_pin11[1]), .pin11(n74245_8_pin11[0]));
  _7404 #(.ShowInternalStructure("true")) u_7404_1 (
    .pin1(n74283_2_pin5[7]), .pin2(n74245_8_pin11[7]), .pin3(n74283_2_pin5[5]), .pin4(n74245_8_pin11[5]),
    .pin5(n74283_2_pin5[3]), .pin6(n74245_8_pin11[3]), .pin13(n74283_2_pin5[6]), .pin12(n74245_8_pin11[6]),
    .pin11(n74283_2_pin5[4]), .pin10(n74245_8_pin11[4]), .pin9(n74283_2_pin5[2]), .pin8(n74245_8_pin11[2]));
  not not_9 (n74245_8_pin11[1], n74283_2_pin5[1]);
  not not_10 (n74245_8_pin11[0], n74283_2_pin5[0]);
  // also tied to GND on the sheet: {n74245_1_pin1, n74245_2_pin1, n74245_4_pin1, n7485_2_pin2, n7485_2_pin4, n74245_5_pin1, n74245_6_pin1, n74245_7_pin1, n74245_8_pin1}
  // also tied to VCC on the sheet: {n74138_1_pin6, n7485_2_pin3}
endmodule
